# Fritzing sketch AIoT-NIDS Circuit Scheme (saved by Fritzing 0.9.10b)
breadboards: 1

parts:
  M1 = DOIT Esp32 DevKit v1 (30 pins long, 11 pins width) [part_number=ESP32S-PIN30]
  HC-SR04_Sensor_1 = HC-SR04 Ultrasonic Distance Sensor
  S1 = Pushbutton [package="[THT]"]
  LED1 = LED - 3mm [color="Red (633nm)" current=0.030 package="3 mm [THT]"]
  R1 = Resistor [tolerance=±5% power=0.25 resistance=220 package=THT]

nets:
  3V3: M1.3V3, HC-SR04_Sensor_1.VCC
  GND: M1.GND, HC-SR04_Sensor_1.GND, S1.Pin_3, S1.Pin_4, R1.Pin_0
  N1: M1.D2, LED1.anode
  N2: M1.D4, S1.Pin_1, S1.Pin_2
  N3: M1.D5, HC-SR04_Sensor_1.TRIG
  N4: M1.D18, HC-SR04_Sensor_1.ECHO
  N5: LED1.cathode, R1.Pin_1

custom parts:
  DOIT Esp32 DevKit v1 (30 pins long, 11 pins width): The DOIT Esp32 DevKit v1 is one of the development board created by DOIT to evaluate the ESP-WROOM-32 module. It is based on the ESP32 microcontroller that boasts Wifi, Bluetooth, Ethernet and Low Power support all in a single chip. (vanepp) made breadboard work, adjusted pin numbering and labels and reduced size of schematic and cleaned up pcb. This chip is 30pins long (2 x15) and 11 pins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
