# Fritzing sketch IoT Proje Devre Şeması (saved by Fritzing 0.9.10b)
breadboards: 1

parts:
  M1 = esp32_p30_w11 [part_number=ESP32S-PIN30]
  HC-SR04_Sensor_1 = HC-SR04 Ultrasonic Distance Sensor
  R1 = Resistor [tolerance=±5% power=0.25 resistance=220 package=THT]
  LED1 = LED - 5mm [color="Red (633nm)" current=0.030 package="5 mm [THT]"]

nets:
  N1: M1.connector0, HC-SR04_Sensor_1.VCC
  N2: M1.connector1, HC-SR04_Sensor_1.GND, R1.Pin_0
  N3: M1.connector3, LED1.anode
  N4: M1.connector7, HC-SR04_Sensor_1.TRIG
  N5: M1.connector8, HC-SR04_Sensor_1.ECHO
  N6: R1.Pin_1, LED1.cathode
